// Logisim project first.circ as structural Verilog: 2 circuits, main circuit ODV_1bit
module ODV_1bit (
  input  A,
  input  B,
  input  B_in,
  output D,
  output B_out
);

  wire and_1_out, and_2_out, and_3_out, and_4_out, and_5_out, and_6_out, and_7_out, not_1_out, not_2_out,
       not_3_out;

  not not_1 (not_1_out, A);
  not not_2 (not_2_out, B);
  not not_3 (not_3_out, B_in);
  and and_1 (and_1_out, not_1_out, not_2_out, B_in);
  and and_2 (and_2_out, not_1_out, B, not_3_out);
  and and_3 (and_3_out, A, not_2_out, not_3_out);
  and and_4 (and_4_out, A, B, B_in);
  and and_5 (and_5_out, not_1_out, B_in);
  and and_6 (and_6_out, not_1_out, B);
  and and_7 (and_7_out, B, B_in);
  or or_1 (D, and_1_out, and_2_out, and_3_out, and_4_out);
  or or_2 (B_out, and_5_out, and_6_out, and_7_out);
endmodule

module ODV_8bit (
  input  [7:0] A,
  input  [7:0] B,
  output [7:0] out_3,
  output B_out
);

  wire odv_1bit_1_b_out, odv_1bit_2_b_out, odv_1bit_3_b_out, odv_1bit_4_b_out, odv_1bit_5_b_out,
       odv_1bit_6_b_out, odv_1bit_8_b_out;

  ODV_1bit odv_1bit_1 (.A(A[0]), .B(B[0]), .B_in(1'b0), .D(out_3[0]), .B_out(odv_1bit_1_b_out));
  ODV_1bit odv_1bit_2 (.A(A[2]), .B(B[2]), .B_in(odv_1bit_8_b_out), .D(out_3[2]), .B_out(odv_1bit_2_b_out));
  ODV_1bit odv_1bit_3 (.A(A[3]), .B(B[3]), .B_in(odv_1bit_2_b_out), .D(out_3[3]), .B_out(odv_1bit_3_b_out));
  ODV_1bit odv_1bit_4 (.A(A[4]), .B(B[4]), .B_in(odv_1bit_3_b_out), .D(out_3[4]), .B_out(odv_1bit_4_b_out));
  ODV_1bit odv_1bit_5 (.A(A[5]), .B(B[5]), .B_in(odv_1bit_4_b_out), .D(out_3[5]), .B_out(odv_1bit_5_b_out));
  ODV_1bit odv_1bit_6 (.A(A[6]), .B(B[6]), .B_in(odv_1bit_5_b_out), .D(out_3[6]), .B_out(odv_1bit_6_b_out));
  ODV_1bit odv_1bit_7 (.A(A[7]), .B(B[7]), .B_in(odv_1bit_6_b_out), .D(out_3[7]), .B_out(B_out));
  ODV_1bit odv_1bit_8 (.A(A[1]), .B(B[1]), .B_in(odv_1bit_1_b_out), .D(out_3[1]), .B_out(odv_1bit_8_b_out));
endmodule
