// Logisim project second.circ as structural Verilog: 3 circuits, main circuit Dec_5421
module Dec_5421 (
  input  I3,
  input  I2,
  input  I1,
  input  I0,
  output O3,
  output O2,
  output O1,
  output O0
);

  wire and_1_out, and_2_out, and_3_out, and_4_out, and_5_out, and_6_out, and_7_out, and_8_out, and_9_out,
       and_10_out, not_1_out, not_2_out, not_3_out, not_4_out;

  not not_1 (not_1_out, I3);
  not not_2 (not_2_out, I2);
  not not_3 (not_3_out, I1);
  not not_4 (not_4_out, I0);
  and and_1 (and_1_out, I3, I2);
  and and_2 (and_2_out, I3, I1, I0);
  and and_3 (and_3_out, not_1_out, I2);
  and and_4 (and_4_out, I3, not_2_out, not_3_out);
  and and_5 (and_5_out, I3, not_2_out, not_4_out);
  and and_6 (and_6_out, not_1_out, I1);
  and and_7 (and_7_out, I3, not_3_out, I0);
  and and_8 (and_8_out, I3, I1, not_4_out);
  and and_9 (and_9_out, not_1_out, I0);
  and and_10 (and_10_out, I3, not_4_out);
  or or_1 (O3, and_1_out, and_2_out);
  or or_2 (O2, and_3_out, and_4_out, and_5_out);
  or or_3 (O1, and_6_out, and_7_out, and_8_out);
  or or_4 (O0, and_9_out, and_10_out);
endmodule

module Enc_5421 (
  input  S4,
  input  S3,
  input  S2,
  input  S1,
  input  S0,
  output T0,
  output U3,
  output U2,
  output U1,
  output U0
);

  wire not_1_out, not_2_out, not_3_out, not_4_out, not_5_out, or_1_out, or_2_out, or_3_out, or_4_out,
       or_5_out, or_6_out, or_7_out, or_8_out, or_9_out, or_10_out, or_11_out, or_12_out, or_13_out,
       or_14_out, or_15_out, or_16_out, or_17_out, or_18_out, or_19_out, or_20_out, or_21_out, or_22_out,
       or_23_out, or_24_out, or_25_out, or_26_out, or_27_out, or_28_out, or_29_out, or_30_out, or_31_out,
       or_32_out, or_33_out, or_34_out, or_35_out;

  not not_1 (not_1_out, S4);
  not not_2 (not_2_out, S3);
  not not_3 (not_3_out, S2);
  not not_4 (not_4_out, S1);
  not not_5 (not_5_out, S0);
  or or_1 (or_1_out, S3, S4);
  or or_2 (or_2_out, S3, not_3_out);
  or or_3 (or_3_out, S1, S2, S4);
  or or_4 (or_4_out, S2, not_2_out, not_1_out);
  or or_5 (or_5_out, S2, S3, S4);
  or or_6 (or_6_out, not_3_out, not_1_out);
  or or_7 (or_7_out, S0, S1, not_3_out);
  or or_8 (or_8_out, S2, S4, not_4_out);
  or or_9 (or_9_out, S0, not_3_out, not_2_out);
  or or_10 (or_10_out, S1, not_3_out, not_2_out);
  or or_11 (or_11_out, S0, S1, not_2_out, not_1_out);
  or or_12 (or_12_out, S2, S3, S4);
  or or_13 (or_13_out, not_5_out, not_3_out);
  or or_14 (or_14_out, S0, S3, not_4_out);
  or or_15 (or_15_out, S0, S3, not_1_out);
  or or_16 (or_16_out, S1, not_5_out, not_1_out);
  or or_17 (or_17_out, S2, not_4_out, not_2_out);
  or or_18 (or_18_out, S0, S1, S4, not_2_out);
  or or_19 (or_19_out, S0, S1, S3);
  or or_20 (or_20_out, S1, S3, S4);
  or or_21 (or_21_out, S1, S3, not_3_out);
  or or_22 (or_22_out, S4, not_4_out, not_2_out);
  or or_23 (or_23_out, S0, S3, S4, not_3_out);
  or or_24 (or_24_out, S0, S2, not_2_out, not_1_out);
  or or_25 (or_25_out, S1, S2, not_5_out, not_2_out);
  or or_26 (or_26_out, S2, S3, not_5_out, not_4_out, not_1_out);
  or or_27 (or_27_out, S0, S1, not_3_out);
  or or_28 (or_28_out, S0, S2, S3, S4);
  or or_29 (or_29_out, S0, not_3_out, not_1_out);
  or or_30 (or_30_out, S2, not_5_out, not_1_out);
  or or_31 (or_31_out, S0, S1, not_2_out, not_1_out);
  or or_32 (or_32_out, S0, S4, not_4_out, not_2_out);
  or or_33 (or_33_out, S1, S2, not_5_out, not_2_out);
  or or_34 (or_34_out, S3, S4, not_5_out, not_3_out);
  or or_35 (or_35_out, S4, not_4_out, not_3_out, not_2_out);
  and and_1 (T0, or_1_out, or_2_out, or_3_out, or_4_out);
  and and_2 (U3, or_5_out, or_6_out, or_7_out, or_8_out, or_9_out, or_10_out, or_11_out);
  and and_3 (U2, or_12_out, or_13_out, or_14_out, or_15_out, or_16_out, or_17_out, or_18_out);
  and and_4 (U1, or_19_out, or_20_out, or_21_out, or_22_out, or_23_out, or_24_out, or_25_out, or_26_out);
  and and_5 (U0, or_27_out, or_28_out, or_29_out, or_30_out, or_31_out, or_32_out, or_33_out, or_34_out, or_35_out);
endmodule

module full (
  input  in_1,
  input  in_2,
  input  in_3,
  input  in_4,
  input  in_5,
  input  in_6,
  input  in_7,
  input  in_8,
  output out_9,
  output out_10,
  output out_11,
  output out_12,
  output out_13,
  output out_14,
  output out_15,
  output out_16
);

  wire [3:0] dec_5421_1_o0, dec_5421_2_o0;
  wire [4:0] adder_1_out, adder_2_out, bit_extender_1_out, bit_extender_2_out;

  Dec_5421 dec_5421_1 (
    .I3(in_1), .I2(in_2), .I1(in_3), .I0(in_4), .O3(dec_5421_1_o0[3]), .O2(dec_5421_1_o0[2]),
    .O1(dec_5421_1_o0[1]), .O0(dec_5421_1_o0[0]));
  Dec_5421 dec_5421_2 (
    .I3(in_5), .I2(in_6), .I1(in_7), .I0(in_8), .O3(dec_5421_2_o0[3]), .O2(dec_5421_2_o0[2]),
    .O1(dec_5421_2_o0[1]), .O0(dec_5421_2_o0[0]));
  assign bit_extender_1_out = {{1{1'b0}}, dec_5421_1_o0};  // Bit_Extender bit_extender_1
  assign bit_extender_2_out = {{1{1'b0}}, dec_5421_2_o0};  // Bit_Extender bit_extender_2
  Adder #(.width(5)) adder_1 (.a(bit_extender_1_out), .b(bit_extender_2_out), .out(adder_1_out));  // open: cin, cout
  Adder #(.width(5)) adder_2 (.a(adder_1_out), .b(5'b01001), .out(adder_2_out));  // open: cin, cout
  Enc_5421 enc_5421_1 (
    .S4(adder_2_out[4]), .S3(adder_2_out[3]), .S2(adder_2_out[2]), .S1(adder_2_out[1]), .S0(adder_2_out[0]),
    .T0(out_12), .U3(out_13), .U2(out_14), .U1(out_15), .U0(out_16));

  assign out_9 = 1'b0;
  assign out_10 = 1'b0;
  assign out_11 = 1'b0;
endmodule
